# Fritzing sketch thruster_schematic (saved by Fritzing 0.9.3b)

parts:
  Jetson_Nano3 = Jetson Nano  # not connected
  VCC2 = Battery
  VCC1 = Battery
  Reg1 = DC-DC CONVERTER [part_number=80633 package=dc-dc_converter]
  M2 = ESC
  920KV_Motor8 = DJI 920 KV Motor
  M3 = ESC
  920KV_Motor9 = DJI 920 KV Motor
  M4 = ESC
  920KV_Motor10 = DJI 920 KV Motor
  M5 = ESC
  920KV_Motor11 = DJI 920 KV Motor
  Reg2 = DC-DC CONVERTER [part_number=80633 package=dc-dc_converter]
  Reg3 = DC-DC CONVERTER [part_number=80633 package=dc-dc_converter]
  Reg4 = DC-DC CONVERTER [part_number=80633 package=dc-dc_converter]
  Part1 = Arduino Mega ADK (Rev3)
  920KV_Motor16 = DJI 920 KV Motor
  920KV_Motor17 = DJI 920 KV Motor
  920KV_Motor18 = DJI 920 KV Motor
  920KV_Motor19 = DJI 920 KV Motor
  M6 = ESC
  M7 = ESC
  M8 = ESC
  M9 = ESC
  Reg5 = DC-DC CONVERTER [part_number=80633 package=dc-dc_converter]

nets:
  N1: VCC2.+, VCC1.+, Reg1.IN+, Reg2.IN+, Reg3.IN+, Reg4.IN+, Reg5.IN+
  N2: VCC1.-, Reg1.IN-, Reg2.IN-, Reg3.IN-, Reg4.IN-, Reg5.IN-
  N3: M2.U, 920KV_Motor8.u
  N4: M2.V, 920KV_Motor8.v
  N5: M2.W, 920KV_Motor8.w
  N6: M2.DATA, Part1.D13_PWM
  GND: M2.GND, M3.GND, M4.GND, M5.GND, Part1.GND
  5V: M2.5V, M3.5V, M4.5V, M5.5V, Part1.5V
  N7: M3.U, 920KV_Motor9.u
  N8: M3.V, 920KV_Motor9.v
  N9: M3.W, 920KV_Motor9.w
  N10: M3.DATA, Part1.D12_PWM
  N11: M4.U, 920KV_Motor10.u
  N12: M4.V, 920KV_Motor10.v
  N13: M4.W, 920KV_Motor10.w
  N14: M4.DATA, Part1.D11_PWM
  N15: M5.U, 920KV_Motor11.u
  N16: M5.V, 920KV_Motor11.v
  N17: M5.W, 920KV_Motor11.w
  N18: M5.DATA, Part1.D10_PWM
  N19: Part1.D9_PWM, M6.DATA
  N20: Part1.D8_PWM, M8.DATA
  N21: Part1.D6_PWM, M9.DATA
  N22: Part1.D7_PWM, M7.DATA
  N23: 920KV_Motor16.w, M9.W
  N24: 920KV_Motor16.v, M9.V
  N25: 920KV_Motor16.u, M9.U
  N26: 920KV_Motor17.w, M8.W
  N27: 920KV_Motor17.v, M8.V
  N28: 920KV_Motor17.u, M8.U
  N29: 920KV_Motor18.w, M6.W
  N30: 920KV_Motor18.v, M6.V
  N31: 920KV_Motor18.u, M6.U
  N32: 920KV_Motor19.w, M7.W
  N33: 920KV_Motor19.v, M7.V
  N34: 920KV_Motor19.u, M7.U

notes:
  usb1

custom parts:
  DC-DC CONVERTER: WYHP 5A constant current/voltage manufactured by Shenzhen Weiyapuhua Technology Co., Ltd
  DJI 920 KV Motor: DJI Brushless Outrunner 2212/920K Motor F330-550
